# Fritzing sketch Heart-Rate-Sensor-Schematic-v0.1.0 (saved by Fritzing 0.9.9b)
breadboards: 1

parts:
  M1 = DOIT Esp32 DevKit v1 (30 pins long, 11 pins width) [part_number=ESP32S-PIN30]
  Display = OLED 0.96" 128x64 I2C SSD1306
  M2 = MakerFocus MAX30102

nets:
  3V3: M1.3V3, Display.VCC, M2.VIN
  GND: M1.GND, Display.GND, M2.GND
  N1: M1.D21, Display.SCA, M2.SDA
  N2: M1.D22, Display.SCL, M2.SCL

custom parts:
  DOIT Esp32 DevKit v1 (30 pins long, 11 pins width): The DOIT Esp32 DevKit v1 is one of the development board created by DOIT to evaluate the ESP-WROOM-32 module. It is based on the ESP32 microcontroller that boasts Wifi, Bluetooth, Ethernet and Low Power support all in a single chip. (vanepp) made breadboard work, adjusted pin numbering and labels and reduced size of schematic and cleaned up pcb. This chip is 30pins long (2 x15) and 11 pins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
  MakerFocus MAX30102: Oximeter module using the MAX30102 chip. As usual, if you want the mounting holes in pcb, you need to drag a hole over the pad in silkscreen to actually drill the hole (by default they are not drilled)
